# Fritzing sketch MEGA2560 (saved by Fritzing 0.8.7b)
breadboards: 1

parts:
  U1 = nRF24L01 [package="DIP8 [THT]"]
  C1 = Electrolytic Capacitor [capacitance=10µF package="0405 [SMD, electrolytic]"]
  元件1 = Sunfounder Mega 2560 (Rev3)

nets:
  N1: U1.connector0, C1.-, 元件1.GND
  N2: U1.connector1, C1.+, 元件1.3V3
  N3: U1.connector2, 元件1.D9_PWM
  N4: U1.connector3, 元件1.D10_PWM
  N5: U1.connector4, 元件1.D13_PWM
  N6: U1.connector5, 元件1.D11_PWM
  N7: U1.connector6, 元件1.D12_PWM
  N8: U1.connector7, 元件1.D8_PWM

notes:
  NRF24L01 Module

custom parts:
  nRF24L01: nrf24l01 wireless module
  Sunfounder Mega 2560 (Rev3): The Arduino Mega 2560 is a microcontroller board based on the ATmega2560 (datasheet). It has 54 digital input/output pins (of which 14 can be used as PWM outputs), 16 analog inputs, 4 UARTs (hardware serial ports), a 16 MHz crystal oscillator, a USB connection, a power jack, an ICSP header, and a reset button. It contains everything needed to support the microcontroller; simply connect it to a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
