# Fritzing sketch UNO (saved by Fritzing 0.8.7b)
breadboards: 1

parts:
  元件1 = Arduino Uno (Rev3) - ICSP
  U1 = nRF24L01 [package="DIP8 [THT]"]
  C1 = Electrolytic Capacitor [capacitance=10µF package="0405 [SMD, electrolytic]"]

nets:
  N1: 元件1.D8, U1.connector7
  N2: 元件1.D9_PWM, U1.connector2
  N3: 元件1.D10_PWM/SS, U1.connector3
  N4: 元件1.D11_PWM/MOSI, U1.connector5
  N5: 元件1.D12/MISO, U1.connector6
  N6: 元件1.D13/SCK, U1.connector4
  N7: 元件1.GND, U1.connector0, C1.-
  N8: 元件1.3V3, U1.connector1, C1.+

notes:
  NRF24L01 Module

custom parts:
  nRF24L01: nrf24l01 wireless module
